// Logisim project 8bit_shifter_ex.circ as structural Verilog: 1 circuit, main circuit main
module main (
  input  D0,
  input  D1,
  input  D2,
  input  D3,
  input  D4,
  input  D5,
  input  D6,
  input  D7,
  input  S0,
  input  S1,
  input  S2,
  output Y0,
  output Y1,
  output Y2,
  output Y3,
  output Y4,
  output Y5,
  output Y6,
  output Y7
);

  wire M0, M1, M2, M3, M4, M5, M6, M7, N0, N1, N2, N3, N4, N5, N6, N7;

  Multiplexer #(.select(1), .enable("false")) multiplexer_1 (.in0(D0), .in1(D1), .out(M0), .sel(S0));
  Multiplexer #(.select(1), .enable("false")) multiplexer_2 (.in0(D1), .in1(D2), .out(M1), .sel(S0));
  Multiplexer #(.select(1), .enable("false")) multiplexer_3 (.in0(D2), .in1(D3), .out(M2), .sel(S0));
  Multiplexer #(.select(1), .enable("false")) multiplexer_4 (.in0(D3), .in1(D4), .out(M3), .sel(S0));
  Multiplexer #(.select(1), .enable("false")) multiplexer_5 (.in0(D4), .in1(D5), .out(M4), .sel(S0));
  Multiplexer #(.select(1), .enable("false")) multiplexer_6 (.in0(D5), .in1(D6), .out(M5), .sel(S0));
  Multiplexer #(.select(1), .enable("false")) multiplexer_7 (.in0(D6), .in1(D7), .out(M6), .sel(S0));
  Multiplexer #(.select(1), .enable("false")) multiplexer_8 (.in0(D7), .in1(D0), .out(M7), .sel(S0));
  Multiplexer #(.select(1), .enable("false")) multiplexer_9 (.in0(M0), .in1(M1), .out(N0), .sel(S1));
  Multiplexer #(.select(1), .enable("false")) multiplexer_10 (.in0(M1), .in1(M2), .out(N1), .sel(S1));
  Multiplexer #(.select(1), .enable("false")) multiplexer_11 (.in0(M2), .in1(M3), .out(N2), .sel(S1));
  Multiplexer #(.select(1), .enable("false")) multiplexer_12 (.in0(M3), .in1(M4), .out(N3), .sel(S1));
  Multiplexer #(.select(1), .enable("false")) multiplexer_13 (.in0(M4), .in1(M5), .out(N4), .sel(S1));
  Multiplexer #(.select(1), .enable("false")) multiplexer_14 (.in0(M5), .in1(M6), .out(N5), .sel(S1));
  Multiplexer #(.select(1), .enable("false")) multiplexer_15 (.in0(M6), .in1(M7), .out(N6), .sel(S1));
  Multiplexer #(.select(1), .enable("false")) multiplexer_16 (.in0(M7), .in1(M0), .out(N7), .sel(S1));
  Multiplexer #(.select(1), .enable("false")) multiplexer_17 (.in0(N0), .in1(N1), .out(Y0), .sel(S2));
  Multiplexer #(.select(1), .enable("false")) multiplexer_18 (.in0(N1), .in1(N2), .out(Y1), .sel(S2));
  Multiplexer #(.select(1), .enable("false")) multiplexer_19 (.in0(N2), .in1(N3), .out(Y2), .sel(S2));
  Multiplexer #(.select(1), .enable("false")) multiplexer_20 (.in0(N3), .in1(N4), .out(Y3), .sel(S2));
  Multiplexer #(.select(1), .enable("false")) multiplexer_21 (.in0(N4), .in1(N5), .out(Y4), .sel(S2));
  Multiplexer #(.select(1), .enable("false")) multiplexer_22 (.in0(N5), .in1(N6), .out(Y5), .sel(S2));
  Multiplexer #(.select(1), .enable("false")) multiplexer_23 (.in0(N6), .in1(N7), .out(Y6), .sel(S2));
  Multiplexer #(.select(1), .enable("false")) multiplexer_24 (.in0(N7), .in1(N0), .out(Y7), .sel(S2));
endmodule
