// Logisim project adder.circ as structural Verilog: 1 circuit, main circuit main
module main (
  input  A,
  input  B,
  input  Cin,
  output Sum,
  output Cout
);

  wire AND_AB, AND_XOR_Cin, XOR_AB;

  xor xor_1 (XOR_AB, A, B);
  xor xor_2 (Sum, XOR_AB, Cin);
  and and_1 (AND_AB, A, B);
  and and_2 (AND_XOR_Cin, XOR_AB, Cin);
  or or_1 (Cout, AND_AB, AND_XOR_Cin);
endmodule
