// Logisim project easy_ex.circ as structural Verilog: 1 circuit, main circuit main
module main (
  input  A,
  input  B,
  input  C,
  output Y
);

  wire A_AND_B, NOT_C;

  and and_1 (A_AND_B, A, B);
  not not_1 (NOT_C, C);
  or or_1 (Y, A_AND_B, NOT_C);
endmodule
