// Logisim project voice_circuit_v24_perfect.circ as structural Verilog: 1 circuit, main circuit main
module main (
  input  CLK,
  input  RST,
  input  EN,
  output Q0,
  output Q1,
  output Q2,
  output Q3,
  output Q4,
  output Q5,
  output Q6,
  output Q7
);

  wire C0, C1, C2, C3, C4, C5, C6, D0, D1, D2, D3, D4, D5, D6, D7;

  xor xor_1 (D0, Q0, EN);
  and and_1 (C0, Q0, EN);
  xor xor_2 (D1, Q1, C0);
  and and_2 (C1, Q1, C0);
  xor xor_3 (D2, Q2, C1);
  and and_3 (C2, Q2, C1);
  xor xor_4 (D3, Q3, C2);
  and and_4 (C3, Q3, C2);
  xor xor_5 (D4, Q4, C3);
  and and_5 (C4, Q4, C3);
  xor xor_6 (D5, Q5, C4);
  and and_6 (C5, Q5, C4);
  xor xor_7 (D6, Q6, C5);
  and and_7 (C6, Q6, C5);
  xor xor_8 (D7, Q7, C6);
  D_Flip_Flop d_ff_1 (.D(D0), .clk(CLK), .Q(Q0), .reset(RST));  // open: Qn, preset
  D_Flip_Flop d_ff_2 (.D(D1), .clk(CLK), .Q(Q1), .reset(RST));  // open: Qn, preset
  D_Flip_Flop d_ff_3 (.D(D2), .clk(CLK), .Q(Q2), .reset(RST));  // open: Qn, preset
  D_Flip_Flop d_ff_4 (.D(D3), .clk(CLK), .Q(Q3), .reset(RST));  // open: Qn, preset
  D_Flip_Flop d_ff_5 (.D(D4), .clk(CLK), .Q(Q4), .reset(RST));  // open: Qn, preset
  D_Flip_Flop d_ff_6 (.D(D5), .clk(CLK), .Q(Q5), .reset(RST));  // open: Qn, preset
  D_Flip_Flop d_ff_7 (.D(D6), .clk(CLK), .Q(Q6), .reset(RST));  // open: Qn, preset
  D_Flip_Flop d_ff_8 (.D(D7), .clk(CLK), .Q(Q7), .reset(RST));  // open: Qn, preset
endmodule
