// Logisim project voice_circuit_v10.circ as structural Verilog: 1 circuit, main circuit main
module main (
  input  A,
  input  B,
  input  S,
  output Y
);

  wire bot, nS, top;

  not not_1 (nS, S);
  and and_1 (top, A, nS);
  and and_2 (bot, B, S);
  or or_1 (Y, top, bot);
endmodule
