// Logisim project voice_circuit_v15_big.circ as structural Verilog: 1 circuit, main circuit main
module main (
  input  A0,
  input  A1,
  input  A2,
  input  EN,
  output Y0,
  output Y1,
  output Y2,
  output Y3,
  output Y4,
  output Y5,
  output Y6,
  output Y7
);

  wire A0_n, A1_n, A2_n;

  not not_1 (A0_n, A0);
  not not_2 (A1_n, A1);
  not not_3 (A2_n, A2);
  and and_1 (Y0, A0_n, A1_n, A2_n, EN);
  and and_2 (Y1, A0, A1_n, A2_n, EN);
  and and_3 (Y2, A0_n, A1, A2_n, EN);
  and and_4 (Y3, A0, A1, A2_n, EN);
  and and_5 (Y4, A0_n, A1_n, A2, EN);
  and and_6 (Y5, A0, A1_n, A2, EN);
  and and_7 (Y6, A0_n, A1, A2, EN);
  and and_8 (Y7, A0, A1, A2, EN);
endmodule
