// Logisim project voice_circuit_v22_patient.circ as structural Verilog: 1 circuit, main circuit main
module main (
  input  in_1,
  input  in_2,
  input  in_3,
  input  in_4,
  input  in_5,
  input  in_6,
  input  in_7,
  input  in_8,
  input  in_9,
  input  in_10,
  input  in_11,
  input  in_12,
  input  in_13,
  input  in_14,
  input  in_15,
  input  in_16,
  input  in_17,
  input  in_18,
  input  in_19,
  input  in_20,
  input  in_21,
  input  in_22,
  input  in_23,
  input  in_24,
  input  in_25,
  input  in_26,
  input  in_27,
  input  in_28,
  input  in_29,
  input  in_30,
  input  in_31,
  input  in_32,
  input  in_33,
  input  in_34,
  input  in_35,
  input  in_36,
  input  in_37,
  input  in_38,
  input  in_39,
  input  in_40,
  input  in_41,
  input  in_42,
  input  in_43,
  input  in_44,
  input  in_45,
  input  in_46,
  input  in_47,
  input  in_48,
  input  in_49,
  input  in_50,
  input  in_51,
  input  in_52,
  input  in_53,
  input  in_54,
  input  in_55,
  input  in_56,
  input  in_57,
  input  in_58,
  input  in_59,
  input  in_60,
  input  in_61,
  input  in_62,
  input  in_63,
  input  in_64,
  input  in_65,
  input  in_66,
  input  in_67,
  input  in_68,
  input  in_69,
  input  in_70,
  input  in_71,
  input  in_72,
  input  in_73,
  input  in_74,
  input  in_75,
  input  in_76,
  input  in_77,
  input  in_78,
  input  in_79,
  input  in_80,
  input  in_81,
  input  in_82,
  input  in_83,
  input  in_84,
  input  in_85,
  input  in_86,
  input  in_87,
  input  in_88,
  input  in_89,
  input  in_90,
  input  in_91,
  input  in_92,
  input  in_93,
  input  in_94,
  input  [1:0] in_95,
  input  in_96,
  input  in_97,
  output out_98,
  output out_99,
  output out_100
);

  and and_1 (out_98, in_1, in_16);
  // OR_Gate or_1 has open pins: in0=in_28, in1=in_40, out=open
  // XOR_Gate xor_1 has open pins: in0=in_48, in1=in_57, out=open
  // NAND_Gate nand_1 has open pins: in0=in_62, in1=in_74, out=open
  // NOR_Gate nor_1 has open pins: in0=in_79, in1=in_92, out=open
  // AND_Gate and_2 has open pins: in0=in_2, in1=in_13, in2=in_23, out=open
  // OR_Gate or_2 has open pins: in0=in_29, in1=in_38, in2=in_45, out=open
  ExactlyOne xor_2 (.in0(in_49), .in1(in_55), .in2(in_60));  // open: out
  // NAND_Gate nand_2 has open pins: in0=in_63, in1=in_71, in2=in_77, out=open
  // NOR_Gate nor_2 has open pins: in0=in_80, in1=in_89, in2=in_96, out=open
  // AND_Gate and_3 has open pins: in0=in_3, in1=in_9, in2=in_17, in3=in_24, out=open
  // OR_Gate or_3 has open pins: in0=in_30, in1=in_35, in2=in_41, in3=in_46, out=open
  ExactlyOne xor_3 (.in0(in_50), .in1(in_53), .in2(in_58), .in3(in_61));  // open: out
  // NAND_Gate nand_3 has open pins: in0=in_64, in1=in_68, in2=in_75, in3=in_78, out=open
  // NOR_Gate nor_3 has open pins: in0=in_81, in1=in_86, in2=in_93, in3=in_97, out=open
  // AND_Gate and_4 has open pins: in0=in_4, in1=in_6, in2=in_10, in3=in_14, in4=in_18, out=open
  // OR_Gate or_4 has open pins: in0=in_31, in1=in_33, in2=in_36, in3=in_39, in4=in_42, out=open
  ExactlyOne xor_4 (.in0(in_51), .in1(in_52), .in2(in_54), .in3(in_56), .in4(in_59));  // open: out
  // NAND_Gate nand_4 has open pins: in0=in_65, in1=in_67, in2=in_69, in3=in_72, in4=in_76, out=open
  // NOR_Gate nor_4 has open pins: in0=in_82, in1=in_84, in2=in_87, in3=in_90, in4=in_94, out=open
  // AND_Gate and_5 has open pins: in0=in_5, in1=in_7, in2=in_11, in3=in_19, in4=in_21, in5=in_25, out=open
  // OR_Gate or_5 has open pins: in0=in_32, in1=in_34, in2=in_37, in3=in_43, in4=in_44, in5=in_47, out=open
  Multiplexer multiplexer_1 (.in0(in_66), .in1(in_70), .out(out_99), .sel(in_73));
  // AND_Gate and_6 has open pins: in0=in_8, in1=in_12, in2=in_15, in3=in_20, in4=in_22, in5=in_26, in6=in_27, out=open
  Multiplexer #(.select(2)) multiplexer_2 (
    .in0(in_83), .in1(in_85), .in2(in_88), .in3(in_91), .out(out_100), .sel(in_95));
endmodule
