// Logisim project voice_circuit_v23_fixed.circ as structural Verilog: 1 circuit, main circuit main
module main (
  input  CLK,
  input  RST,
  input  EN,
  output Q0,
  output Q1,
  output Q2,
  output Q3,
  output Q4,
  output Q5,
  output Q6
);

  wire D0, D1, D2, D3, D4, D5, D6, EFFECTIVE_RST, RESET_CONDITION, RESET_SIGNAL;

  // XOR_Gate xor_1 has open pins: out=D0
  // XOR_Gate xor_2 has open pins: out=D1
  // XOR_Gate xor_3 has open pins: out=D2
  // XOR_Gate xor_4 has open pins: out=D3
  // XOR_Gate xor_5 has open pins: out=D4
  // XOR_Gate xor_6 has open pins: out=D5
  // XOR_Gate xor_7 has open pins: out=D6
  and and_1 (RESET_CONDITION, Q2, Q3, Q4);
  // AND_Gate and_2 has open pins: out=RESET_SIGNAL
  // OR_Gate or_1 has open pins: out=EFFECTIVE_RST
  D_Flip_Flop d_ff_1 (.D(D0), .clk(CLK), .Q(Q0), .reset(EFFECTIVE_RST));  // open: Qn, preset
  D_Flip_Flop d_ff_2 (.D(D1), .clk(CLK), .Q(Q1), .reset(EFFECTIVE_RST));  // open: Qn, preset
  D_Flip_Flop d_ff_3 (.D(D2), .clk(CLK), .Q(Q2), .reset(EFFECTIVE_RST));  // open: Qn, preset
  D_Flip_Flop d_ff_4 (.D(D3), .clk(CLK), .Q(Q3), .reset(EFFECTIVE_RST));  // open: Qn, preset
  D_Flip_Flop d_ff_5 (.D(D4), .clk(CLK), .Q(Q4), .reset(EFFECTIVE_RST));  // open: Qn, preset
  D_Flip_Flop d_ff_6 (.D(D5), .clk(CLK), .Q(Q5), .reset(EFFECTIVE_RST));  // open: Qn, preset
  D_Flip_Flop d_ff_7 (.D(D6), .clk(CLK), .Q(Q6), .reset(EFFECTIVE_RST));  // open: Qn, preset
endmodule
