// Logisim project voice_circuit_v24_perfect.circ as structural Verilog: 1 circuit, main circuit main
module main (
  input  CLK,
  input  RST,
  input  EN,
  output Q0,
  output Q1,
  output Q2,
  output Q3,
  output Q4,
  output Q5,
  output Q6,
  output Q7
);

  wire D0, D1, D2, D3, D4, D5, D6, D7, EN_COUNT, ENABLE, MAX;

  xor xor_1 (D0, Q0, EN);
  xor xor_2 (D1, Q1, D0);
  xor xor_3 (D2, Q2, D1);
  xor xor_4 (D3, Q3, D2);
  xor xor_5 (D4, Q4, D3);
  xor xor_6 (D5, Q5, D4);
  xor xor_7 (D6, Q6, D5);
  xor xor_8 (D7, Q7, D6);
  and and_1 (MAX, Q2, Q3, Q4, Q5);
  not not_1 (ENABLE, MAX);
  and and_2 (EN_COUNT, EN, ENABLE);
  D_Flip_Flop d_ff_1 (.D(D0), .clk(CLK), .Q(Q0), .reset(RST));  // open: Qn, preset
  D_Flip_Flop d_ff_2 (.D(D1), .clk(CLK), .Q(Q1), .reset(RST));  // open: Qn, preset
  D_Flip_Flop d_ff_3 (.D(D2), .clk(CLK), .Q(Q2), .reset(RST));  // open: Qn, preset
  D_Flip_Flop d_ff_4 (.D(D3), .clk(CLK), .Q(Q3), .reset(RST));  // open: Qn, preset
  D_Flip_Flop d_ff_5 (.D(D4), .clk(CLK), .Q(Q4), .reset(RST));  // open: Qn, preset
  D_Flip_Flop d_ff_6 (.D(D5), .clk(CLK), .Q(Q5), .reset(RST));  // open: Qn, preset
  D_Flip_Flop d_ff_7 (.D(D6), .clk(CLK), .Q(Q6), .reset(RST));  // open: Qn, preset
  D_Flip_Flop d_ff_8 (.D(D7), .clk(CLK), .Q(Q7), .reset(RST));  // open: Qn, preset
endmodule
